# Fritzing sketch esquema-eletrico-droidhouse (saved by Fritzing 0.9.2b)
circuit board: 17.4409cm x 14.9925cm
breadboards: 3

parts:
  Componente1 = Arduino Mega 2560 (Rev3)
  T1 = LM35 Temperature Sensor [package="TO92 [THT]"]
  LED2 = smd LED [color="White (6500K)" package="0805 [SMD]"]  # not connected
  Componente2 = Arduino Uno (Rev3)
  K3 = Relay [part_number=FRS1B-S package=THT]
  K4 = Relay [part_number=FRS1B-S package=THT]
  M2 = DC Motor
  D3 = Rectifier Diode [part_number=1N4001 package="300 mil [THT]"]
  D4 = Rectifier Diode [part_number=1N4001 package="300 mil [THT]"]
  Q3 = NPN-Transistor [package="TO92 [THT]"]
  R6 = Resistor [tolerance=±5% resistance=2.2k package=THT]
  R7 = Resistor [tolerance=±5% resistance=2.2k package=THT]
  Q4 = NPN-Transistor [package="TO92 [THT]"]
  24_V1 = Power plug
  Start1 = Pushbutton [package=THT]
  Stop1 = Pushbutton [package=THT]
  Medidor_de_Corrente_ACS712 = ACS712 Low Current Sensor Board v12
  J1 = Screw terminal - 2 pins [package=THT]
  AC_127_~_230_v = Power plug
  Componente3 = songle relay  # not connected

nets:
  N1: Componente1.A0, T1.Vout
  N2: Componente1.A1, Medidor_de_Corrente_ACS712.VO
  GND: Componente1.GND, T1.GND, Medidor_de_Corrente_ACS712.GND
  5V: Componente1.IOREF, Componente1.5V, T1.+Vs, Medidor_de_Corrente_ACS712.5V
  GND_2: Componente2.GND, K3.A, K4.A, Q3.E, Q4.E, 24_V1.GND, Start1.leg1, Stop1.leg1
  N3: Componente2.D0/RX, Start1.leg0
  N4: Componente2.D1/TX, Stop1.leg0
  N5: Componente2.D2, R6.Pin_1
  N6: Componente2.D3_PWM, R7.Pin_0
  N7: K3.COIL1, D3.anode, Q3.C
  N8: K3.C1, K3.C2, M2.pin_1
  N9: K3.COIL2, K4.COIL2, D3.cathode, D4.cathode
  N10: K3.B, K4.B, 24_V1.VCC
  N11: K4.COIL1, D4.anode, Q4.C
  N12: K4.C1, K4.C2, M2.pin_2
  N13: Q3.B, R7.Pin_1
  N14: R6.Pin_0, Q4.B
  N15: Medidor_de_Corrente_ACS712.IP-, AC_127_~_230_v.GND
  N16: Medidor_de_Corrente_ACS712.IP+, J1.pin2
  N17: J1.pin1, AC_127_~_230_v.VCC

notes:
  24 V motor
  12 V coil (relay)

// code stored in the sketch: andruino.ino
/**
 * =========================================================================
 *
 * App: Andruino
 * Versão: 0.0.1
 * Data: 23 de julho de 2015
 * Developer: Rodrigues F. A. S.
 *
 * ======================================================================*/

 #include <Thread.h>
 #include <ThreadController.h>

 /* Declara uma thread "raiz" um controle que agrupa as thread's filhas.. */
 ThreadController cpu;
 Thread threadRecebeDadosandroid;

 /* Pino que conecta os pinos do LED RGB. */
 const int VERMELHO = 10;
 const int VERDE = 9;
 const int AZUL = 11;

 /* Tempo de cor de transição. */
 const int delayTime = 10;

 /* Definição de variáveis globais. */
 int ValVermelho = 0;
 int ValAzul = 0;
 int ValVerde = 0;

 boolean separador = false;
 const uint8_t BUFFER = 15;
 char dispositivo[BUFFER];
 uint8_t tamDispositivo = 0;
 char valor[5];
 uint8_t tamValor = 0;
 int aux = 0;

/**
 * setup -
 */
 void setup() {
  /* Inicia uma comunicação serial com uma taxa de 9600, para comunicação via Bluetooth.. */
  Serial.begin(9600);

  /* Define o pino digital como saída. */
  pinMode(VERDE, OUTPUT);
  pinMode(AZUL, OUTPUT);
  pinMode(VERMELHO, OUTPUT);

  threadRecebeDadosandroid.setInterval(15);
  threadRecebeDadosandroid.onRun(recebeDadosAndroid);

  /* Adiciona as thread's filhas a thread raiz ou mãe.. */
  cpu.add(&threadRecebeDadosandroid);
}

/**
 * loop -
 */
 void loop() {
  /* Start a thread raiz.. */
  cpu.run();
}

/**
 * recebeDadosAndroid -
 */
 void recebeDadosAndroid() {
  if(Serial.available()) { /* Enquanto houverem bytes disponíveis; */
    char c = Serial.read(); /* Lê byte do buffer serial; */
    
    if (c == '\n') {
      if (tamDispositivo == 0) return;
      dispositivo[tamDispositivo] = 0;
      tamDispositivo = 0;

      valor[tamValor] = 0;
      tamValor = 0;

      aux = atoi(valor);
      separador = false;
      
      if (!strcmp(dispositivo, "led_on") && !strcmp(valor, "1")) led_on();
      else if (!strcmp(dispositivo, "led_off") && !strcmp(valor, "0")) led_off();
      else if (!strcmp(dispositivo, "seekBarR")) analogWrite(VERMELHO, ValVermelho = aux);
      else if (!strcmp(dispositivo, "seekBarG")) analogWrite(VERDE, ValVerde = aux);
      else if (!strcmp(dispositivo, "seekBarB")) analogWrite(AZUL, ValAzul = aux);
      else if (!strcmp(dispositivo, "demoRGB")) demoRGB();
    }
    else if (tamDispositivo < BUFFER - 1) { // Verifica, separa e incrementa os dados.
      if(c != '+' && separador == false){
        dispositivo[tamDispositivo] = c;
        tamDispositivo++;        
      }
      else if(c == '+'){
        separador = true;
      } 
      else {
        valor[tamValor] = c;
        tamValor++;
      }
    }
  }
}

/**
 * led_on -
 */
 void led_on() {
  digitalWrite(VERDE, HIGH); digitalWrite(AZUL, HIGH); digitalWrite(VERMELHO, HIGH);
}

/**
 * led_off -
 */
 void led_off() {
  digitalWrite(VERDE, LOW); digitalWrite(AZUL, LOW); digitalWrite(VERMELHO, LOW);
}

 /**
  * demoRGB - 
  */
  void demoRGB(){
    /** 
  * ==============================================
  * Variação de VERDE para VERMELHO
  * ================================= 
  */
  int ValVermelho = 255;
  int ValAzul = 0;
  int ValVerde = 0;

  for(int i = 0 ; i < 255 ; i += 1) {
    ValVerde += 1;
    ValVermelho -= 1;

    /** 
     * Em cada ciclo de diferença 
     * 255 - ValVerde Redução 
     * 255 - ValVermelho Aumenta
     * Calsando uma transição gradual de VERDE para VERMELHO 
     */

     analogWrite( VERDE, 255 - ValVerde );  
     analogWrite( VERMELHO, 255 - ValVermelho );

     /* Aguardando para perceber cor */
     delay( delayTime );
  } // FIM for

/** 
  * ==============================================
  * Variação de AZUL para VERDE
  * ================================= 
  */

  ValVermelho = 0;  
  ValAzul = 0;  
  ValVerde = 255;

  for(int i = 0 ; i < 255 ; i += 1){
    ValAzul += 1;  
    ValVerde -= 1;

    /** 
     * Em cada ciclo de diferença 
     * 255 - ValAzul Redução 
     * 255 - ValVerde Aumenta 
     * Calsando uma transição gradual de AZUL para VERDE.
     */

     analogWrite( AZUL, 255 - ValAzul );  
     analogWrite( VERDE, 255 - ValVerde );

     /* Aguardando para perceber cor */
     delay( delayTime );  
   }  

/** 
  * ==============================================
  * Variação de VERMELHO para AZUL
  * ================================= 
  */ 
  ValVermelho = 0;  
  ValAzul = 255;  
  ValVerde = 0;  
  
  for( int i = 0 ; i < 255 ; i += 1 ){  
    ValVermelho += 1;  
    ValAzul -= 1;

    /**
     * Em cada ciclo de diferença 
     * 255 - ValVermelho Redução 
     * 255 - ValAzul Aumenta 
     * Calsando uma transição gradual de VERMELHO para AZUL.
     */
     analogWrite( VERMELHO, 255 - ValVermelho );  
     analogWrite( AZUL, 255 - ValAzul );

     /* Aguardando para perceber cor */
     delay( delayTime );  
   }  
 }
